# Fritzing sketch Circuit (saved by Fritzing 0.9.2b)
breadboards: 1

parts:
  C1 = Electrolytic Capacitor [capacitance=1µF package="100 mil [THT, electrolytic]"]
  U1 = LIPO-110mAh [package=lipo-110]
  VCC1 = Battery block 9V  # not connected
  Q1 = NPN-Transistor [package="TO92 [THT]"]
  Q2 = NPN-Transistor [package="TO92 [THT]"]
  U2 = atmega168 [package=dip]
  Handy = screw terminal, 2 pins
  GSM_SIM_GPSR_SMS_SIM900_SIM1 = SIM800L [package=THT]  # not connected

nets:
  N1: C1.-, U1.+
  N2: C1.+, U1.-, Q1.E, Q2.E
  N3: U2.D0_(RX), Handy.pin2
  N4: U2.D1_(TX), Handy.pin1
